# Fritzing sketch block-diagram (saved by Fritzing 0.8.7b)
breadboards: 1

parts:
  Part1 = Arduino Uno (Rev3)
  Part2 = SRF05 Ultrasonic Rangefinder
  J1 = Basic Servo

nets:
  N1: Part1.D9_PWM, J1.pulse
  N2: Part1.D12/MISO, Part2.Echo
  N3: Part1.D13/SCK, Part2.Trig
  VCC: Part1.5V, Part2.VCC, J1.vcc
  GND: Part1.GND, Part2.GND, J1.gnd
